// Logisim project cpu.circ as structural Verilog: 1 circuit, main circuit cpu
module cpu (
  input  clk,
  input  [31:0] INSTRUCTION,
  input  [31:0] READ_DATA,
  output [31:0] WRITE_ADDRESS,
  output [31:0] PROGRAM_COUNTER,
  output [31:0] ra,
  output [31:0] sp,
  output [31:0] t0,
  output [31:0] t1,
  output [31:0] t2,
  output [31:0] s0,
  output [31:0] s1,
  output [31:0] a0,
  output [31:0] tohost,
  output [3:0] WRITE_ENABLE,
  output [31:0] WRITE_DATA
);

  wire PCSel, RegWen;
  wire [1:0] WBSel;
  wire [2:0] ImmSel;
  wire [3:0] ALUSel;
  wire [4:0] AddrA, AddrB, AddrD;
  wire [31:0] adder_1_out, ALU_OUT, DataA, DataB, IF_PIPED, IMM;

  Adder #(.width(32)) adder_1 (.a(PROGRAM_COUNTER), .b(32'h4), .out(adder_1_out));  // open: cin, cout
  Register #(.width(32)) PC (.D(adder_1_out), .clk(clk), .Q(PROGRAM_COUNTER));  // open: en, clr
  Register #(.width(32)) IF_Reg (
    .D(INSTRUCTION), .clk(clk), .Q({IF_PIPED[31:25], AddrB, AddrA, IF_PIPED[14:12], AddrD, IF_PIPED[6:0]}));  // open: en, clr
  imm_gen imm_gen_1 (
    .inst({IF_PIPED[31:25], AddrB, AddrA, IF_PIPED[14:12], AddrD, IF_PIPED[6:0]}), .ImmSel(ImmSel), .imm(IMM));
  control_logic control_logic_1 (
    .PCSel(PCSel), .RegWEn(RegWen), .ImmSel(ImmSel), .ALUSel(ALUSel), .WBSel(WBSel),
    .inst({IF_PIPED[31:25], AddrB, AddrA, IF_PIPED[14:12], AddrD, IF_PIPED[6:0]}));  // open: CSRWen, BrUn, ASel, BSel, MemRW, CSRSel, BrEq, BrLt
  regfile regfile_1 (
    .rs1(AddrA), .rs2(AddrB), .rd(AddrD), .Write_Data(ALU_OUT), .RegWEn(RegWen), .clk(clk), .ra(ra), .sp(sp),
    .t0(t0), .t1(t1), .t2(t2), .s0(s0), .s1(s1), .a0(a0), .Read_Data_1(DataA), .Read_Data_2(DataB));
  // branch_comp branch_comp_1: pin names not known
  alu alu_1 (.Result(ALU_OUT), .A(DataA), .B(IMM), .ALUSel(ALUSel));
  // csr csr_1: pin names not known; wires that end beside it: tohost

  // Other names for the same wires on the sheet: IF_PIPED (some bits) = {AddrB, AddrA, AddrD}; WBVal[31:0] = ALU_OUT

  // Notes on the sheet:
  //   Output to IMEM
  //   IMEM (do **NOT** move this)
  //   Inputs from IMEM
  //   It is OK to move the PC, RegFile, ALU, MEM, Branch Comp, Imm Gen, and Control Logic to wherever is most convenient for you when constructing your CPU, and to delete this text
  //   Inputs/Outputs for testing. Do **NOT** move these.
  //   Outputs To DMEM
  //   DMEM (do **NOT** move this)
  //   Inputs From DMEM
endmodule
